# Fritzing sketch MotionCamera (saved by Fritzing 0.9.5d)
breadboards: 1

parts:
  Raspberry_Pi_3_Model_B = Raspberry Pi 3 [part_number=RPI-3-V1.2]
  RPI_HC-SR501 = PIR sensor
  LED1 = smd LED [color="Red (633nm)" package="0805 [SMD]"]
  LED2 = smd LED [color="Red (633nm)" package="1206 [SMD]"]
  R1 = Resistor [tolerance=±5% resistance=220 package="0603 [SMD]"]
  R2 = Resistor [tolerance=±5% resistance=220 package="0603 [SMD]"]

nets:
  N1: Raspberry_Pi_3_Model_B.GND, LED1.cathode, LED2.cathode
  N2: Raspberry_Pi_3_Model_B.GPIO24, R2.Pin_1
  N3: Raspberry_Pi_3_Model_B.GPIO23, RPI_HC-SR501.SIG, R1.Pin_1
  5V: Raspberry_Pi_3_Model_B.5V, RPI_HC-SR501.VDD
  N4: LED1.anode, R1.Pin_0
  N5: LED2.anode, R2.Pin_0

notes:
  Place "Raspberry Pi Camera Module V2" into camera-slot
  Pick yellow color for LED2
